// Logisim project Guess the Number Xtreme.circ as structural Verilog: 13 circuits, main circuit somador4b
module somador4b (
  input  [3:0] in_1,
  input  [3:0] in_2,
  output [4:0] out_3
);

  Adder #(.width(4)) adder_1 (.a(in_1), .b(in_2), .out(out_3[3:0]), .cout(out_3[4]));  // open: cin
endmodule

module comparador5b (
  input  [4:0] in_1,
  input  [4:0] in_2,
  output out_3,
  output out_4,
  output out_5
);

  wire and_1_out, and_2_out, and_3_out, and_4_out, and_5_out, and_6_out, and_7_out, and_8_out,
       comp1b_1_out_3, comp1b_1_out_4, comp1b_1_out_5, comp1b_2_out_3, comp1b_2_out_4, comp1b_2_out_5,
       comp1b_3_out_3, comp1b_3_out_4, comp1b_3_out_5, comp1b_4_out_3, comp1b_4_out_4, comp1b_4_out_5,
       comp1b_5_out_3, comp1b_5_out_4, comp1b_5_out_5;

  comp1b comp1b_1 (.a(in_1[0]), .b(in_2[0]), .out_3(comp1b_1_out_3), .out_4(comp1b_1_out_4), .out_5(comp1b_1_out_5));
  comp1b comp1b_2 (.a(in_1[1]), .b(in_2[1]), .out_3(comp1b_2_out_3), .out_4(comp1b_2_out_4), .out_5(comp1b_2_out_5));
  comp1b comp1b_3 (.a(in_1[4]), .b(in_2[4]), .out_3(comp1b_3_out_3), .out_4(comp1b_3_out_4), .out_5(comp1b_3_out_5));
  comp1b comp1b_4 (.a(in_1[3]), .b(in_2[3]), .out_3(comp1b_4_out_3), .out_4(comp1b_4_out_4), .out_5(comp1b_4_out_5));
  comp1b comp1b_5 (.a(in_1[2]), .b(in_2[2]), .out_3(comp1b_5_out_3), .out_4(comp1b_5_out_4), .out_5(comp1b_5_out_5));
  and and_1 (and_1_out, comp1b_3_out_3, comp1b_4_out_4);
  and and_2 (and_2_out, comp1b_3_out_3, comp1b_4_out_3, comp1b_5_out_4);
  and and_3 (and_3_out, comp1b_3_out_3, comp1b_4_out_3, comp1b_5_out_3, comp1b_2_out_4);
  and and_4 (and_4_out, comp1b_3_out_3, comp1b_4_out_3, comp1b_5_out_3, comp1b_2_out_3, comp1b_1_out_4);
  and and_5 (and_5_out, comp1b_3_out_3, comp1b_4_out_5);
  and and_6 (and_6_out, comp1b_3_out_3, comp1b_4_out_3, comp1b_5_out_5);
  and and_7 (and_7_out, comp1b_3_out_3, comp1b_4_out_3, comp1b_5_out_3, comp1b_2_out_5);
  and and_8 (and_8_out, comp1b_3_out_3, comp1b_4_out_3, comp1b_5_out_3, comp1b_2_out_3, comp1b_1_out_5);
  and and_9 (out_3, comp1b_3_out_3, comp1b_4_out_3, comp1b_5_out_3, comp1b_2_out_3, comp1b_1_out_3);
  or or_1 (out_4, comp1b_3_out_4, and_1_out, and_4_out, and_2_out, and_3_out);
  or or_2 (out_5, comp1b_3_out_5, and_5_out, and_8_out, and_6_out, and_7_out);
endmodule

module comparador4b (
  input  [3:0] in_1,
  input  [3:0] in_2,
  output out_3,
  output out_4,
  output out_5
);

  wire and_1_out, and_2_out, and_3_out, and_4_out, and_5_out, and_6_out, comp1b_1_out_3, comp1b_1_out_4,
       comp1b_1_out_5, comp1b_2_out_3, comp1b_2_out_4, comp1b_2_out_5, comp1b_3_out_3, comp1b_3_out_4,
       comp1b_3_out_5, comp1b_4_out_3, comp1b_4_out_4, comp1b_4_out_5;

  comp1b comp1b_1 (.a(in_1[3]), .b(in_2[3]), .out_3(comp1b_1_out_3), .out_4(comp1b_1_out_4), .out_5(comp1b_1_out_5));
  comp1b comp1b_2 (.a(in_1[2]), .b(in_2[2]), .out_3(comp1b_2_out_3), .out_4(comp1b_2_out_4), .out_5(comp1b_2_out_5));
  comp1b comp1b_3 (.a(in_1[1]), .b(in_2[1]), .out_3(comp1b_3_out_3), .out_4(comp1b_3_out_4), .out_5(comp1b_3_out_5));
  comp1b comp1b_4 (.a(in_1[0]), .b(in_2[0]), .out_3(comp1b_4_out_3), .out_4(comp1b_4_out_4), .out_5(comp1b_4_out_5));
  and and_1 (and_1_out, comp1b_1_out_3, comp1b_2_out_4);
  and and_2 (and_2_out, comp1b_2_out_3, comp1b_1_out_3, comp1b_3_out_4);
  and and_3 (and_3_out, comp1b_1_out_3, comp1b_3_out_3, comp1b_4_out_4, comp1b_2_out_3);
  and and_4 (and_4_out, comp1b_1_out_3, comp1b_2_out_5);
  and and_5 (and_5_out, comp1b_1_out_3, comp1b_2_out_3, comp1b_3_out_5);
  and and_6 (and_6_out, comp1b_1_out_3, comp1b_2_out_3, comp1b_3_out_3, comp1b_4_out_5);
  and and_7 (out_3, comp1b_2_out_3, comp1b_1_out_3, comp1b_3_out_3, comp1b_4_out_3);
  or or_1 (out_4, comp1b_1_out_4, and_1_out, and_2_out, and_3_out);
  or or_2 (out_5, comp1b_1_out_5, and_4_out, and_5_out, and_6_out);
endmodule

module diff5b (
  input  [4:0] in_1,
  input  [4:0] in_2,
  output [4:0] out_3
);

  wire subtrator1b_1_bout, subtrator1b_2_bout, subtrator1b_3_bout, subtrator1b_4_bout;

  subtrator1b subtrator1b_1 (.a(in_1[0]), .b(in_2[0]), .bin(1'b0), .diff(out_3[0]), .bout(subtrator1b_1_bout));
  subtrator1b subtrator1b_2 (
    .a(in_1[1]), .b(in_2[1]), .bin(subtrator1b_1_bout), .diff(out_3[1]), .bout(subtrator1b_2_bout));
  subtrator1b subtrator1b_3 (
    .a(in_1[2]), .b(in_2[2]), .bin(subtrator1b_2_bout), .diff(out_3[2]), .bout(subtrator1b_3_bout));
  subtrator1b subtrator1b_4 (
    .a(in_1[3]), .b(in_2[3]), .bin(subtrator1b_3_bout), .diff(out_3[3]), .bout(subtrator1b_4_bout));
  subtrator1b subtrator1b_5 (.a(in_1[4]), .b(in_2[4]), .bin(subtrator1b_4_bout), .diff(out_3[4]));  // open: bout
endmodule

module subtrator1b (
  input  a,
  input  b,
  input  bin,
  output diff,
  output bout
);

  wire and_1_out, and_2_out, and_3_out, xor_1_out;

  xor xor_1 (xor_1_out, a, b);
  and and_1 (and_1_out, b, bin);
  and and_2 (and_2_out, ~a, bin);  // AND_Gate
  and and_3 (and_3_out, ~a, b);  // AND_Gate
  xor xor_2 (diff, xor_1_out, bin);
  or or_1 (bout, and_1_out, and_2_out, and_3_out);
endmodule

// cores
module cores5b (
  input  [4:0] num,
  output [7:0] vermelho,
  output [7:0] azul
);

  assign vermelho = ~{num, {3{num[4]}}};  // NOT_Gate not_1, 8 bits wide

  assign azul = {num, {3{num[4]}}};
endmodule

module mux1b (
  input  a,
  input  b,
  input  c,
  output x
);

  wire and_1_out, and_2_out, not_1_out;

  not not_1 (not_1_out, a);
  and and_1 (and_1_out, not_1_out, b);
  and and_2 (and_2_out, a, c);
  or or_1 (x, and_1_out, and_2_out);
endmodule

module diffmux5b (
  input  [4:0] x,
  input  [4:0] y,
  output [4:0] out_3
);

  wire comparador5b_1_out_3;
  wire [4:0] mux5b_1_out_4, mux5b_2_out_4;

  comparador5b comparador5b_1 (.in_1(x), .in_2(y), .out_3(comparador5b_1_out_3));  // open: out_4, out_5
  mux5b mux5b_1 (.a(y), .b(x), .chave(comparador5b_1_out_3), .out_4(mux5b_1_out_4));
  diff5b diff5b_1 (.in_1(mux5b_1_out_4), .in_2(mux5b_2_out_4), .out_3(out_3));
  mux5b mux5b_2 (.a(x), .b(y), .chave(comparador5b_1_out_3), .out_4(mux5b_2_out_4));
endmodule

module mux5b (
  input  [4:0] a,
  input  [4:0] b,
  input  chave,
  output [4:0] out_4
);

  mux1b mux1b_1 (.a(chave), .b(a[4]), .c(b[4]), .x(out_4[4]));
  mux1b mux1b_2 (.a(chave), .b(a[3]), .c(b[3]), .x(out_4[3]));
  mux1b mux1b_3 (.a(chave), .b(a[2]), .c(b[2]), .x(out_4[2]));
  mux1b mux1b_4 (.a(chave), .b(a[1]), .c(b[1]), .x(out_4[1]));
  mux1b mux1b_5 (.a(chave), .b(a[0]), .c(b[0]), .x(out_4[0]));
endmodule

module comp1b (
  input  a,
  input  b,
  output out_3,
  output out_4,
  output out_5
);

  wire and_1_out, and_2_out, not_1_out, not_2_out, not_3_out, not_4_out;

  not not_1 (not_1_out, a);
  not not_2 (not_2_out, b);
  not not_3 (not_3_out, b);
  not not_4 (not_4_out, a);
  and and_1 (and_1_out, not_1_out, not_2_out);
  and and_2 (and_2_out, a, b);
  and and_3 (out_4, a, not_3_out);
  and and_4 (out_5, not_4_out, b);
  or or_1 (out_3, and_1_out, and_2_out);
endmodule

module maquina_de_estados (
  output out_1,
  output out_2,
  output out_3,
  output out_4
);

  D_Flip_Flop d_ff_1 ();  // open: clk, D, Q, Qn, preset, reset
  D_Flip_Flop d_ff_2 ();  // open: clk, D, Q, Qn, preset, reset
endmodule

module GTN_X (
  input  Confirmar,
  input  Novo,
  input  [3:0] x,
  input  [3:0] y,
  output [7:0] VERMELHO,
  output [7:0] AZUL,
  output X_CERTO,
  output Y_CERTO,
  output SOMA_CERTA
);

  wire comp4b_2_out_3, comp4b_out_3, comp5b_out_3;
  wire [4:0] diffmux_out_3, soma4b_2_out_3, soma4b_out_3;
  wire [7:0] bit_extender_1_out, cores5b_1_azul, cores5b_1_vermelho, random_1_out;

  Random random_1 (.clk(Novo), .out(random_1_out));  // open: next, clr
  assign bit_extender_1_out = {{7{Confirmar}}, Confirmar};  // Bit_Extender bit_extender_1
  somador4b soma4b (.in_1(random_1_out[7:4]), .in_2(random_1_out[3:0]), .out_3(soma4b_out_3));
  somador4b soma4b_2 (.in_1(x), .in_2(y), .out_3(soma4b_2_out_3));
  and and_1 (X_CERTO, Confirmar, comp4b_out_3);
  comparador4b comp4b (.in_1(random_1_out[3:0]), .in_2(x), .out_3(comp4b_out_3));  // open: out_4, out_5
  and and_2 (Y_CERTO, Confirmar, comp4b_2_out_3);
  comparador4b comp4b_2 (.in_1(random_1_out[7:4]), .in_2(y), .out_3(comp4b_2_out_3));  // open: out_4, out_5
  and and_3 (SOMA_CERTA, Confirmar, comp5b_out_3);
  comparador5b comp5b (.in_1(soma4b_out_3), .in_2(soma4b_2_out_3), .out_3(comp5b_out_3));  // open: out_4, out_5
  assign VERMELHO = bit_extender_1_out & cores5b_1_vermelho;  // AND_Gate and_4, 8 bits wide
  diffmux5b diffmux (.x(soma4b_out_3), .y(soma4b_2_out_3), .out_3(diffmux_out_3));
  assign AZUL = cores5b_1_azul & bit_extender_1_out;  // AND_Gate and_5, 8 bits wide
  cores5b cores5b_1 (.num(diffmux_out_3), .vermelho(cores5b_1_vermelho), .azul(cores5b_1_azul));
endmodule

module teste (
  input  [3:0] in_1,
  input  [3:0] in_2,
  output out_3,
  output out_4,
  output out_5
);

  wire button_1_out, button_2_out;
  wire [7:0] rgbled_1_p1, rgbled_1_p2;

  Button button_1 (.out(button_1_out));
  Button button_2 (.out(button_2_out));
  // RGBLed #(.multibit("true")) rgbled_1: pin names not known; wires that end beside it: rgbled_1_p1, rgbled_1_p2
  GTN_X gtn_x_1 (
    .Confirmar(button_1_out), .Novo(button_2_out), .x(in_1), .y(in_2), .X_CERTO(out_3), .Y_CERTO(out_4),
    .SOMA_CERTA(out_5), .VERMELHO(rgbled_1_p1), .AZUL(rgbled_1_p2));
endmodule
